# Fritzing sketch RP2040-Rangefinder (saved by Fritzing 1.0.5)
breadboards: 1

parts:
  OLED1 = OLED 128x64 I2C Monochrome Display GND-VDD
  A1 = Waveshare rp2040-zero smd [package=SMD]
  HC-SR04_Sensor_1 = HC-SR04 Ultrasonic Distance Sensor

nets:
  GND: OLED1.GND, A1.Pin_2, A1.Pin_33, HC-SR04_Sensor_1.GND
  VDD: OLED1.VDD, A1.Pin_3, HC-SR04_Sensor_1.VCC
  N1: OLED1.SCK, A1.Pin_18
  N2: OLED1.SDA, A1.Pin_19
  N3: A1.Pin_6, HC-SR04_Sensor_1.TRIG
  N4: A1.Pin_17, HC-SR04_Sensor_1.ECHO

notes:
  距離センサーモジュール
  OLED モジュール
  RP2040-Zero
  ブレッドボード 170H

custom parts:
  OLED 128x64 I2C Monochrome Display GND-VDD: OLED 128x64 I2C Monochrome Display. Note: there are two variants of this part, this one is the GND VDD SCK SDA variant. The other is VDD GND SCK SDA. Make sure you select the part that matches your module as using the incorrect part will probably destroy your module! In addition the mounting holes are marked on silkscreen but not by default drilled. If you want drilled mounting holes, copy a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
  Waveshare rp2040-zero smd: .RP2040-Zero, A Low-Cost, High-Performance Pico-Like MCU Board Based On Raspberry Pi Microcontroller RP2040. This varant is SMD with all the connections.
